# Fritzing sketch schematics (saved by Fritzing 0.7.4b)
breadboards: 1

parts:
  J1 = Basic Force Sensing Resistor (FSR) [package=THT]
  J2 = Basic Force Sensing Resistor (FSR) [package=THT]
  J3 = Basic Force Sensing Resistor (FSR) [package=THT]
  J4 = Basic Force Sensing Resistor (FSR) [package=THT]
  J5 = Basic Force Sensing Resistor (FSR) [package=THT]
  J6 = Basic Force Sensing Resistor (FSR) [package=THT]
  Arduino1 = Arduino
  R1 = Resistor [tolerance=±5% resistance=1M package=THT]
  R2 = Resistor [tolerance=±5% resistance=1M package=THT]
  R4 = Resistor [tolerance=±5% resistance=1M package=THT]
  R5 = Resistor [tolerance=±5% resistance=1M package=THT]
  R6 = Resistor [tolerance=±5% resistance=1M package=THT]
  R3 = Resistor [tolerance=±5% resistance=1M package=THT]

nets:
  N1: J1.pin_0, Arduino1.A0, R1.Pin_0
  N2: J1.pin_1, J2.pin_1, J3.pin_1, J4.pin_1, J5.pin_1, J6.pin_1, Arduino1.GND, R1.Pin_1, R2.Pin_1, R4.Pin_1, R5.Pin_1, R6.Pin_1, R3.Pin_1
  N3: J2.pin_0, Arduino1.A1, R2.Pin_0
  N4: J3.pin_0, Arduino1.A2, R3.Pin_0
  N5: J4.pin_0, Arduino1.A3, R4.Pin_0
  N6: J5.pin_0, Arduino1.A4, R5.Pin_0
  N7: J6.pin_0, Arduino1.A5, R6.Pin_0
